// Logisim project alu.circ as structural Verilog: 1 circuit, main circuit main
module main (
  input  [15:0] X,
  input  [15:0] Y,
  input  [2:0] switch__S,
  output signed_overflow,
  output [15:0] result,
  output equal
);
endmodule
