// Logisim project cpu.circ as structural Verilog: 1 circuit, main circuit main
module main (
  input  [15:0] From_Instr_Mem,
  input  clk,
  output [15:0] r0,
  output [15:0] r1,
  output [15:0] r2,
  output [15:0] r3,
  output [15:0] Display_0,
  output [15:0] Display_1,
  output [15:0] To_Instr_Mem,
  output [15:0] Data_Mem_Data,
  output [15:0] Data_Mem_Addr,
  output Data_Mem_Write
);


  // Other names for the same wires on the sheet: d0[15:0] = Display_0; d1[15:0] = Display_1
endmodule
